# Fritzing sketch DoBot_interface (saved by Fritzing 0.9.9b)
breadboards: 1

parts:
  U1 = ESP32S-HiLetgo [part_number=ESP32S-HiLetgo]
  Part1 = Adafruit TCS34725 RGB Color Sensor [part_number="Adafruit #1334"]
  LED1 = smd LED [color="Red (633nm)" package="0805 [SMD]"]
  LED3 = smd LED [color="Red (633nm)" package="0805 [SMD]"]
  S1 = Momentary Switch [package=ksa_sealed_tac_switch]
  Part2 = KY-033 Tracing Black White Line Hunting Sensor Module For Arduino
  J1 = Camdenboss CTB0158-6 [part_number=CTB0158-6 package=THT]
  LED2 = smd LED [color="Red (633nm)" package="0805 [SMD]"]

nets:
  N1: U1.3.3, Part1.+3V3
  N2: U1.GPIO34, J1.pin1
  N3: U1.GPIO35, J1.pin2
  N4: U1.GPIO32, Part2.S
  N5: U1.GPIO25, S1.1
  N6: U1.GPIO26, J1.pin6
  GND: U1.GND, Part1.GND, LED1.cathode, LED3.cathode, LED2.cathode
  N7: U1.GPIO13, LED1.anode
  VIN: U1.VIN, Part1.VIN, S1.4, Part2.GND, Part2.V+
  N8: U1.GPIO4, LED2.anode
  N9: U1.GPIO16, J1.pin5
  N10: U1.GPIO17, J1.pin4
  N11: U1.GPIO18, J1.pin3
  N12: U1.GPIO21, Part1.SDA
  N13: U1.GPIO22, Part1.SCL
  N14: U1.GPIO23, LED3.anode

custom parts:
  ESP32S-HiLetgo: HiLetgo ESP-WROOM-32 ESP32 ESP-32S Development Board 2.4GHz Dual-Mode WiFi + Bluetooth Dual Cores Microcontroller The ESP32 integrated with Antenna switches, RF Balun, power amplifiers, low-noise amplifiers, filters, and management modules, and the entire solution occupies the least area of PCB. 2.4 GHz Wi-Fi plus Bluetooth dual-mode chip, with TSMC Ultra-low power consumption 40nm technology,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
  Adafruit TCS34725 RGB Color Sensor: Your electronics can now see in dazzling color with this lovely color light sensor. We found the best color sensor on the market, the TCS34725, which has RGB and Clear light sensing elements. An IR blocking filter, integrated on-chip and localized to the color sensing photodiodes, minimizes the IR spectral component of the incoming light and allows color measurements to be made accurately. The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
  KY-033 Tracing Black White Line Hunting Sensor Module For Arduino: Tracing Black White Line Hunting Sensor Module For Arduino Description: This is KY-033 tracking sensor. The KY-033 measures the intensity of infrared radiation and delivers it as an analog output voltage. Features: Operating voltage: 2.5 - 12V(cannot over12V) working current: 18mA-20mA at 5V Enhanced accuracy Documents: http://www.vishay.com/docs/83760/tcrt5000.pdf
